// Logisim project Main.circ as structural Verilog: 1 circuit, main circuit main
module main (
);

  wire clock_1_out, RESET_IP_out;
  wire [7:0] adder_1_out, IP_q;

  Clock clock_1 (.out(clock_1_out));
  Register IP (.D(adder_1_out), .en(1'b1), .clk(clock_1_out), .Q(IP_q), .clr(RESET_IP_out));
  Adder adder_1 (.a(8'h1), .b(IP_q), .out(adder_1_out));  // open: cin, cout
  Button RESET_IP (.out(RESET_IP_out));
  ROM #(.dataWidth(24)) MI (.addr(IP_q));  // open: data
endmodule
